# Fritzing sketch Perfboard (saved by Fritzing 0.8.7b)
circuit board: 8.46667cm x 5.64444cm
stripboards: 1

parts:
  D2 = Diode [package=diode-1n4148]
  U1 = mystery part, 3 pins [chip_label=UP/DOWN]
  VCC1 = 4 x AAA Battery Mount  # not connected
  U2 = mystery part, 4 pins [chip_label=GPS]
  U3 = mystery part, 4 pins [chip_label=POWER]
  J1 = female pin header, 5 pins [form="♀ (female)"]
  R1 = Resistor [tolerance=±5% resistance=330 package=THT]
  R2 = Resistor [tolerance=±5% resistance=10k package=THT]
  R3 = Resistor [tolerance=±5% resistance=10k package=THT]
  U4 = Voltage Regulator - 3.3V [package="TO220 [THT]"]
  J2 = Basic Servo
  C1 = Capacitor [package=cap-pth-small-kit]
  C2 = Electrolytic Capacitor [capacitance=100µF package="200 mil [THT, electrolytic]"]  # not connected
  Q1 = NPN-Transistor [part_number=2N3906 package="TO92 [THT]"]
  J3 = female pin header, 10 pins [form="♀ (female)"]
  D3 = Diode [package=diode-1n4148]

nets (from the pcb view):
  N1: D2.A, J1.pin1
  N2: D2.C, U1.pin3, D3.C
  N3: U1.pin1, U4.input_voltage, Q1.C, J3.pin1
  GND: U1.pin2, U2.pin2, J1.pin5, R2.Pin_0, R3.Pin_1, U4.GND, J2.gnd, C1.2, J3.pin2
  N4: U2.pin1, U4.output_voltage, C1.1
  N5: U2.pin4, J3.pin3
  N6: U3.pin2, D3.A
  N7: U3.pin4, R2.Pin_1, J3.pin6
  N8: J1.pin2, J3.pin9
  N9: J1.pin3, J3.pin10
  N10: R1.Pin_0, J3.pin7
  N11: R1.Pin_1, R3.Pin_0, Q1.B
  N12: J2.vcc, Q1.E
  N13: J2.pulse, J3.pin5
