# Fritzing sketch PuzzleBox (saved by Fritzing 0.8.7b)
circuit board: 8.46667cm x 5.64444cm
breadboards: 1

parts:
  Part1 = Arduino Uno (Rev3)
  U1 = LCD-16X2 [package=lcd-16x2]
  J1 = Basic Servo
  VCC1 = 4 x AAA Battery Mount
  U2 = mystery part, 3 pins [chip_label=? part_number=POWER]
  Q1 = PNP-Transistor [package="SOT-23 [SMD]"]
  U3 = VENUS634 [package=lga44]
  U4 = mystery part, 3 pins [chip_label=? part_number="STEP-UP / STEP-DOWN"]
  Q2 = NPN-Transistor [package="TO92 [THT]"]
  U5 = Voltage Regulator - 3.3V [package="TO220 [THT]"]
  C2 = Ceramic Capacitor [capacitance="100 nF" package="1206 [SMD, multilayer]"]
  J2 = female pin header, 5 pins [form="♀ (female)"]
  R1 = Resistor [tolerance=±5% resistance=10k package=THT]
  R2 = Resistor [tolerance=±5% resistance=330 package=THT]
  C3 = Electrolytic Capacitor [capacitance=10µF package="100 mil [THT, electrolytic]"]
  C4 = Electrolytic Capacitor [capacitance=0.1mF package="100 mil [THT, electrolytic]"]
  D1 = Diode [package=diode-1n4001]
  D2 = Diode [package=diode-1n4001]

nets:
  N1: Part1.A0, J2.pin2
  N2: Part1.A1, J2.pin3
  N3: Part1.D8, U1.DB7
  N4: Part1.D9_PWM, Q2.B
  N5: Part1.D11_PWM/MOSI, J1.pulse
  N6: Part1.D12/MISO, R2.Pin_0
  N7: Part1.D13/SCK, U2.pin2
  GND: Part1.GND, U1.VSS, U1.DB0, U1.DB1, U1.DB2, U1.DB3, U1.K, J1.gnd, VCC1.+, U3.GNDRF, U4.pin2, U5.GND, C2.0, J2.pin5, R1.Pin_0, C3.-, C4.-
  N8: Part1.D0/RX, U3.TX
  N9: Part1.D2, U1.RS
  N10: Part1.D3_PWM, U1.R_W
  N11: Part1.D4, U1.E
  N12: Part1.D5_PWM, U1.DB4
  N13: Part1.D6_PWM, U1.DB5
  N14: Part1.D7, U1.DB6
  5V: Part1.5V, U1.VDD, Q1.2, U4.pin1, Q2.C, U5.input_voltage, C4.+
  N15: U1.A, Q2.E
  N16: J1.vcc, Q1.1
  N17: VCC1.-, D2.A
  N18: U2.pin1, U4.pin3
  8V: U2.pin3, D1.C, D2.C
  N19: Q1.0, R1.Pin_1, R2.Pin_1
  N20: U3.VCC, U5.output_voltage, C2.1, C3.+
  N21: J2.pin1, D1.A
